# Fritzing sketch SEMEN-UNO-WATCH (saved by Fritzing 0.9.5d)

parts:
  Part1 = Arduino Pro Mini V2 (5V)
  LCD1 = LCD screen
  R1 = Resistor [tolerance=±5% resistance=220 package="0402 [SMD]"]
  DS1302 = Real Time Clock Module - DS1302 RTC Breakout Board
  C2 = Electrolytic Capacitor [capacitance=10µF voltage=16V package="100 mil [THT, electrolytic]"]
  RE1 = Rotary Encoder [package=THT]
  S1 = Momentary Switch [package=ksa_sealed_tac_switch]
  ZS-042_RTC1 = DS3231 AT24C32 Real Time Clock
  Part2 = Arduino Pro Mini V2 (5V)

nets:
  GND: Part1.GND, LCD1.VSS, LCD1.LED-, DS1302.GND, C2.-, RE1.EncoderPinC, S1.2
  VCC: Part1.VCC, LCD1.VDD, DS1302.5V
  N1: Part1.A3, DS1302.DAT
  N2: Part1.A2, DS1302.CLK
  N3: Part1.A1, DS1302.RST
  N4: Part1.MISO, S1.4
  N5: Part1.MOSI, RE1.EncoderPinA
  N6: Part1.D10, RE1.EncoderPinB
  N7: Part1.D9, LCD1.LED+
  N8: Part1.D8, LCD1.DB7
  N9: Part1.D7, LCD1.DB6
  N10: Part1.D6, LCD1.DB5
  N11: Part1.D5, LCD1.DB4
  N12: Part1.D4, LCD1.E
  N13: Part1.D3, R1.Pin_1
  N14: Part1.D2, LCD1.RS
  N15: R1.Pin_0, C2.+
  N16: ZS-042_RTC1.SCL, Part2.A5
  N17: ZS-042_RTC1.SDA, Part2.A4
  VCC_2: ZS-042_RTC1.VCC, Part2.VCC
  GND_2: ZS-042_RTC1.GND, Part2.GND

custom parts:
  Arduino Pro Mini V2 (5V): Arduino Pro Mini V2 There are several different layouts for this board out there. This one is modeled after the Sparkfun 11113 board but a few of the pins have been moved around.
  Real Time Clock Module - DS1302 RTC Breakout Board: This a custom designed module for the DS1307 Real Time Clock. The module comes fully assembled and pre-programmed with the current time (ok, so it's our current time - MST). The included Lithium coin cell battery (CR1225 41mAh) will run the module for a minimum of 9 years (17 years typical) without external 5V power. The DS1307 is accessed via the I2C protocol. We've written a test-bed to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
  DS3231 AT24C32 Real Time Clock: Real-time clock basedo on chip DS3231, plus memory chip AT24C32 (32 Kb storage capacity). On-chip temperature sensor with an accuracy of ±3 ℃, I2C bus interface maximum speed: 400 kHz. Operating voltage: 3.3 V to 5.5 V with battery backup capabilities.
